# Fritzing sketch fire protection (saved by Fritzing 0.9.3b)

parts:
  LCD1 = LCD screen
  MQ2 = GAS_SENSOR [package=mq-3]
  MQ2_2 = GAS_SENSOR [package=mq-3]
  MQ2_3 = GAS_SENSOR [package=mq-3]
  RHT1 = Humidity and Temperature Sensor RHT03
  Part1 = Arduino Nano (Rev3.0) (ICSP)
  J2 = Power Jack [package=power_jack_pth_lock]
  J4 = Generic male header - 3 pins [form="♂ (male)" package=THT]
  S2 = KY-026
  S3 = KY-026
  S4 = KY-026
  LCM1602_IIC1 = LCM1602 IIC [part_number="LCM1602 IIC" chip_label="LCM1602 IIC" package="DIP (Dual Inline) [THT]"]
  J6 = Generic male header - 3 pins [form="♂ (male)" package=THT]
  J7 = Power Jack [package=power_jack_pth_lock]
  WeMos_D1_Mini1 = WeMos D1 Mini
  U1 = 2-Channel 5v Relay Shield [package=relay-2ch5v10a]
  U2 = 4-Channel 5v Relay Shield [package=relay-4ch5v10a]
  J8 = Generic male header - 3 pins [form="♂ (male)" package=THT]
  M1 = DC Motor
  M2 = DC Motor
  M3 = DC Motor
  M4 = RioRand LM2596
  J9 = Piezo Speaker  # not connected
  J10 = Piezo Speaker
  J11 = Piezo Speaker  # not connected
  LED2 = LEDs [package=fkit-led-1206]
  LED3 = LEDs [package=fkit-led-1206]
  LED4 = LEDs [package=fkit-led-1206]

nets:
  VSS: LCD1.VSS, LCM1602_IIC1.VSS
  VDD: LCD1.VDD, LCM1602_IIC1.VDD
  N1: LCD1.V0, LCM1602_IIC1.V0
  N2: LCD1.RS, LCM1602_IIC1.RS
  N3: LCD1.R/W, LCM1602_IIC1.RW
  N4: LCD1.E, LCM1602_IIC1.E
  N5: LCD1.DB0, LCM1602_IIC1.D0
  N6: LCD1.DB1, LCM1602_IIC1.D1
  N7: LCD1.DB2, LCM1602_IIC1.D2
  N8: LCD1.DB3, LCM1602_IIC1.D3
  N9: LCD1.DB4, LCM1602_IIC1.D4
  N10: LCD1.DB5, LCM1602_IIC1.D5
  N11: LCD1.DB6, LCM1602_IIC1.D6
  N12: LCD1.DB7, LCM1602_IIC1.D7
  N13: LCD1.LED+, LCM1602_IIC1.A
  N14: LCD1.LED-, LCM1602_IIC1.K
  N15: MQ2.B1, Part1.A0
  N16: MQ2_2.B1, Part1.A2
  N17: MQ2_3.B1, Part1.A6
  N18: RHT1.Data-signal, Part1.D13/SCK
  N19: RHT1.GND_2, J10.pin1
  N20: Part1.D2, U2.IN1
  N21: Part1.D3, U2.IN2
  N22: Part1.D4, U2.IN3
  N23: Part1.D5, WeMos_D1_Mini1.D1
  N24: Part1.D6, WeMos_D1_Mini1.D2
  N25: Part1.D7, U2.IN4
  N26: Part1.D8, U1.IN1
  N27: Part1.D9, U1.IN2
  VIN: Part1.VIN, LCM1602_IIC1.VCC, WeMos_D1_Mini1.5V
  N28: Part1.A7, S4.pin1
  N29: Part1.A5, LCM1602_IIC1.SCL
  N30: Part1.A4, LCM1602_IIC1.SDA
  N31: Part1.A3, S3.pin1
  N32: Part1.A1, S2.pin1
  N33: J2.GND, M4.Pin_2
  N34: J2.PWR, M4.Pin_1
  N35: J4.pin1, U2.K1-On
  N36: LCM1602_IIC1.GND, WeMos_D1_Mini1.G
  N37: LCM1602_IIC1.LED_A, LCM1602_IIC1.LED_B
  N38: J6.pin1, U2.K2-On
  N39: J6.pin2, J6.pin3
  N40: J7.GND, M3.pin_1
  N41: J7.PWR, U2.K1-Off
  N42: U1.K1-Off, LED3.A
  N43: U1.K1-On, M2.pin_2
  N44: U1.K2-Off, LED2.A
  N45: U1.K2-On, M3.pin_2
  N46: U2.K3-On, J8.pin1
  N47: U2.K4-In, LED4.A
  N48: U2.K4-On, M1.pin_2

custom parts:
  Generic male header - 3 pins: Generic male header
  KY-026: ky-026 flame sensor module
  LCM1602 IIC: I2C-Module to use a 1602 or 2004 LCD on with the wire.h libory Serial LCD Modul
  2-Channel 5v Relay Shield: 2 Channel 5v Relay Shield w. 2x SPD-06VDC-SD-C
  4-Channel 5v Relay Shield: 4 Channel 5v Relay Shield w. 2x SPD-06VDC-SD-C
